# Fritzing sketch bt.to.ipod.dock (saved by Fritzing 0.9.2b)
circuit board: 8.46667cm x 5.64444cm
breadboards: 1

parts:
  Part1 = Purpletooth Jamboree!!
  U1 = iPod Female Connector [package=ipod_female_connector]
  Teensy_3_1 = Teensy 3.0 [part_number="Freescale ARM MK20DX128"]
  U2 = Voltage Regulator - 5V [package="TO220 [THT]"]
  50mA = Resettable Fuse PTC [package=0603]

nets:
  N1: Part1.TXO, Teensy_3_1.0
  N2: Part1.RXI, Teensy_3_1.1
  GND: Part1.GND, U1.GND, Teensy_3_1.GND, U2.GND
  VCC: Part1.VCC, Teensy_3_1.Vin, U2.output_voltage
  R_OUT: Part1.R_OUT, U1.RIGHT_OUT
  L_OUT: Part1.L_OUT, U1.LEFT_OUT
  N3: U1.TX, Teensy_3_1.10
  N4: U1.RX, Teensy_3_1.9
  N5: U1.3.3V, 50mA.2
  N6: U1.FW_12V, U2.input_voltage
  N7: Teensy_3_1.3.3V, 50mA.1

notes:
  12v power ground actually connected to ipod connector pin 29 but this fritzing item does not have this pin
